# Fritzing sketch dance of light (saved by Fritzing 0.9.4)
breadboards: 1

parts:
  Part1 = Arduino Uno (Rev3)
  S1 = Pushbutton [package="[THT]"]
  LED1 = LED - 5mm [color="Green (565nm)" package="5 mm [THT]"]
  LED2 = LED - 5mm [color="Green (565nm)" package="5 mm [THT]"]
  LED3 = LED - 5mm [color="Green (565nm)" package="5 mm [THT]"]
  LED4 = LED - 5mm [color="Green (565nm)" package="5 mm [THT]"]
  R2 = Resistor [tolerance=±5% resistance=180 package="1206 [SMD]"]
  R3 = Resistor [tolerance=±5% resistance=180 package="1206 [SMD]"]
  R4 = Resistor [tolerance=±5% resistance=180 package="1206 [SMD]"]
  R5 = Resistor [tolerance=±5% resistance=180 package="1206 [SMD]"]
  R6 = Resistor [tolerance=±5% resistance=10k package=THT]

nets:
  N1: Part1.D8, S1.Pin_1, S1.Pin_2, R6.Pin_1
  N2: Part1.GND, S1.Pin_3, S1.Pin_4, LED1.cathode, LED2.cathode, LED3.cathode, LED4.cathode
  N3: Part1.D0/RX, R2.Pin_0
  N4: Part1.D1/TX, R3.Pin_0
  N5: Part1.D2, R4.Pin_0
  N6: Part1.D3_PWM, R5.Pin_0
  N7: Part1.5V, R6.Pin_0
  N8: LED1.anode, R2.Pin_1
  N9: LED2.anode, R3.Pin_1
  N10: LED3.anode, R4.Pin_1
  N11: LED4.anode, R5.Pin_1
